// Logisim project fibCounter1010.circ as structural Verilog: 2 circuits, main circuit main
module main (
  input  in_1
);

  wire clock_1_out, comparator_1_eq;
  wire [0:0] adder_1_out_3, adder_1_out_4, adder_1_out_5, adder_1_out_6, adder_1_out_7, adder_1_out_8,
       adder_1_out_9, adder_1_out_10, adder_1_out_11, adder_1_out_12, adder_1_out_13, cmp_4_add_3_5_out,
       cmp_4_add_3_7_out, cmp_4_add_3_8_out, cmp_4_add_3_10_out, cmp_4_add_3_11_out, cmp_4_add_3_13_out,
       cmp_4_add_3_14_out, cmp_4_add_3_17_out, cmp_4_add_3_18_out, cmp_4_add_3_21_out, cmp_4_add_3_22_out,
       cmp_4_add_3_23_out, cmp_4_add_3_25_out, cmp_4_add_3_26_out, cmp_4_add_3_27_out, cmp_4_add_3_28_out,
       cmp_4_add_3_29_out, cmp_4_add_3_30_out, cmp_4_add_3_31_out, cmp_4_add_3_33_out, cmp_4_add_3_34_out;
  wire [2:0] cmp_4_add_3_1_out, cmp_4_add_3_3_out, cmp_4_add_3_3_out_2, cmp_4_add_3_5_out_2,
       cmp_4_add_3_7_out_2, cmp_4_add_3_8_out_2, cmp_4_add_3_10_out_2, cmp_4_add_3_11_out_2,
       cmp_4_add_3_13_out_2, cmp_4_add_3_14_out_2, cmp_4_add_3_17_out_2, cmp_4_add_3_18_out_2,
       cmp_4_add_3_21_out_2, cmp_4_add_3_22_out_2, cmp_4_add_3_23_out_2, cmp_4_add_3_25_out_2,
       cmp_4_add_3_26_out_2, cmp_4_add_3_27_out_2, cmp_4_add_3_28_out_2, cmp_4_add_3_29_out_2,
       cmp_4_add_3_30_out_2, cmp_4_add_3_31_out_2, cmp_4_add_3_33_out_2, cmp_4_add_3_34_out_2;
  wire [3:0] adder_1_out_2, cmp_4_add_3_4_out, cmp_4_add_3_6_out, cmp_4_add_3_9_out, cmp_4_add_3_12_out,
       cmp_4_add_3_15_out, cmp_4_add_3_16_out, cmp_4_add_3_19_out, cmp_4_add_3_20_out, cmp_4_add_3_24_out,
       cmp_4_add_3_32_out;
  wire [15:0] register_1_q, register_2_q;
  wire [15:12] adder_1_out;

  Clock clock_1 (.out(clock_1_out));
  Register #(.width(16)) register_1 (
    .D(register_2_q), .Q(register_1_q), .clk(clock_1_out), .clr(comparator_1_eq));  // open: en
  Adder #(.width(16)) adder_1 (
    .a(register_1_q), .b(register_2_q),
    .out({adder_1_out, adder_1_out_2[0], adder_1_out_3[0], adder_1_out_4[0], adder_1_out_5[0], adder_1_out_6[0], adder_1_out_7[0], adder_1_out_8[0], adder_1_out_9[0], adder_1_out_10[0], adder_1_out_11[0], adder_1_out_12[0], adder_1_out_13[0]}),
    .cin(in_1));  // open: cout
  cmp_4_add_3 cmp_4_add_3_1 (.in({1'b0, adder_1_out[15:13]}), .out({cmp_4_add_3_3_out[2], cmp_4_add_3_1_out}));
  Register #(.width(16)) register_2 (
    .D({adder_1_out, adder_1_out_2[0], adder_1_out_3[0], adder_1_out_4[0], adder_1_out_5[0], adder_1_out_6[0], adder_1_out_7[0], adder_1_out_8[0], adder_1_out_9[0], adder_1_out_10[0], adder_1_out_11[0], adder_1_out_12[0], adder_1_out_13[0]}),
    .Q(register_2_q), .clk(clock_1_out), .clr(comparator_1_eq));  // open: en
  cmp_4_add_3 cmp_4_add_3_2 (
    .in({cmp_4_add_3_1_out, adder_1_out[12]}), .out({cmp_4_add_3_3_out[1], adder_1_out_2[3:1]}));
  cmp_4_add_3 cmp_4_add_3_3 (.in(adder_1_out_2), .out({cmp_4_add_3_3_out[0], cmp_4_add_3_3_out_2}));
  cmp_4_add_3 cmp_4_add_3_4 (.in({1'b0, cmp_4_add_3_3_out}), .out(cmp_4_add_3_4_out));
  cmp_4_add_3 cmp_4_add_3_5 (
    .in({cmp_4_add_3_3_out_2, adder_1_out_3[0]}), .out({cmp_4_add_3_5_out[0], cmp_4_add_3_5_out_2}));
  cmp_4_add_3 cmp_4_add_3_6 (.in({cmp_4_add_3_4_out[2:0], cmp_4_add_3_5_out[0]}), .out(cmp_4_add_3_6_out));
  Comparator #(.width(16)) comparator_1 (
    .a({adder_1_out, adder_1_out_2[0], adder_1_out_3[0], adder_1_out_4[0], adder_1_out_5[0], adder_1_out_6[0], adder_1_out_7[0], adder_1_out_8[0], adder_1_out_9[0], adder_1_out_10[0], adder_1_out_11[0], adder_1_out_12[0], adder_1_out_13[0]}),
    .b(16'h2ac2), .eq(comparator_1_eq));  // open: gt, lt
  cmp_4_add_3 cmp_4_add_3_7 (
    .in({cmp_4_add_3_5_out_2, adder_1_out_4[0]}), .out({cmp_4_add_3_7_out[0], cmp_4_add_3_7_out_2}));
  cmp_4_add_3 cmp_4_add_3_8 (
    .in({cmp_4_add_3_6_out[2:0], cmp_4_add_3_7_out[0]}), .out({cmp_4_add_3_8_out[0], cmp_4_add_3_8_out_2}));
  cmp_4_add_3 cmp_4_add_3_9 (
    .in({1'b0, cmp_4_add_3_4_out[3], cmp_4_add_3_6_out[3], cmp_4_add_3_8_out[0]}), .out(cmp_4_add_3_9_out));
  cmp_4_add_3 cmp_4_add_3_10 (
    .in({cmp_4_add_3_7_out_2, adder_1_out_5[0]}), .out({cmp_4_add_3_10_out[0], cmp_4_add_3_10_out_2}));
  cmp_4_add_3 cmp_4_add_3_11 (
    .in({cmp_4_add_3_8_out_2, cmp_4_add_3_10_out[0]}), .out({cmp_4_add_3_11_out[0], cmp_4_add_3_11_out_2}));
  cmp_4_add_3 cmp_4_add_3_12 (.in({cmp_4_add_3_9_out[2:0], cmp_4_add_3_11_out[0]}), .out(cmp_4_add_3_12_out));
  cmp_4_add_3 cmp_4_add_3_13 (
    .in({cmp_4_add_3_10_out_2, adder_1_out_6[0]}), .out({cmp_4_add_3_13_out[0], cmp_4_add_3_13_out_2}));
  cmp_4_add_3 cmp_4_add_3_14 (
    .in({cmp_4_add_3_11_out_2, cmp_4_add_3_13_out[0]}), .out({cmp_4_add_3_14_out[0], cmp_4_add_3_14_out_2}));
  cmp_4_add_3 cmp_4_add_3_15 (.in({cmp_4_add_3_12_out[2:0], cmp_4_add_3_14_out[0]}), .out(cmp_4_add_3_15_out));
  cmp_4_add_3 cmp_4_add_3_16 (
    .in({1'b0, cmp_4_add_3_9_out[3], cmp_4_add_3_12_out[3], cmp_4_add_3_15_out[3]}), .out(cmp_4_add_3_16_out));
  cmp_4_add_3 cmp_4_add_3_17 (
    .in({cmp_4_add_3_13_out_2, adder_1_out_7[0]}), .out({cmp_4_add_3_17_out[0], cmp_4_add_3_17_out_2}));
  cmp_4_add_3 cmp_4_add_3_18 (
    .in({cmp_4_add_3_14_out_2, cmp_4_add_3_17_out[0]}), .out({cmp_4_add_3_18_out[0], cmp_4_add_3_18_out_2}));
  cmp_4_add_3 cmp_4_add_3_19 (.in({cmp_4_add_3_15_out[2:0], cmp_4_add_3_18_out[0]}), .out(cmp_4_add_3_19_out));
  cmp_4_add_3 cmp_4_add_3_20 (.in({cmp_4_add_3_16_out[2:0], cmp_4_add_3_19_out[3]}), .out(cmp_4_add_3_20_out));
  cmp_4_add_3 cmp_4_add_3_21 (
    .in({cmp_4_add_3_17_out_2, adder_1_out_8[0]}), .out({cmp_4_add_3_21_out[0], cmp_4_add_3_21_out_2}));
  cmp_4_add_3 cmp_4_add_3_22 (
    .in({cmp_4_add_3_18_out_2, cmp_4_add_3_21_out[0]}), .out({cmp_4_add_3_22_out[0], cmp_4_add_3_22_out_2}));
  cmp_4_add_3 cmp_4_add_3_23 (
    .in({cmp_4_add_3_19_out[2:0], cmp_4_add_3_22_out[0]}), .out({cmp_4_add_3_23_out[0], cmp_4_add_3_23_out_2}));
  cmp_4_add_3 cmp_4_add_3_24 (.in({cmp_4_add_3_20_out[2:0], cmp_4_add_3_23_out[0]}), .out(cmp_4_add_3_24_out));
  Hex_Digit_Display hex_digit_display_1 (.value({cmp_4_add_3_16_out[3], cmp_4_add_3_20_out[3], cmp_4_add_3_24_out[3], cmp_4_add_3_29_out[0]}));  // open: dp
  cmp_4_add_3 cmp_4_add_3_25 (
    .in({cmp_4_add_3_21_out_2, adder_1_out_9[0]}), .out({cmp_4_add_3_25_out[0], cmp_4_add_3_25_out_2}));
  cmp_4_add_3 cmp_4_add_3_26 (
    .in({cmp_4_add_3_22_out_2, cmp_4_add_3_25_out[0]}), .out({cmp_4_add_3_26_out[0], cmp_4_add_3_26_out_2}));
  cmp_4_add_3 cmp_4_add_3_27 (
    .in({cmp_4_add_3_26_out_2, cmp_4_add_3_30_out[0]}), .out({cmp_4_add_3_27_out[0], cmp_4_add_3_27_out_2}));
  cmp_4_add_3 cmp_4_add_3_28 (
    .in({cmp_4_add_3_23_out_2, cmp_4_add_3_26_out[0]}), .out({cmp_4_add_3_28_out[0], cmp_4_add_3_28_out_2}));
  cmp_4_add_3 cmp_4_add_3_29 (
    .in({cmp_4_add_3_24_out[2:0], cmp_4_add_3_28_out[0]}), .out({cmp_4_add_3_29_out[0], cmp_4_add_3_29_out_2}));
  Hex_Digit_Display hex_digit_display_2 (.value({cmp_4_add_3_29_out_2, cmp_4_add_3_32_out[3]}));  // open: dp
  cmp_4_add_3 cmp_4_add_3_30 (
    .in({cmp_4_add_3_25_out_2, adder_1_out_10[0]}), .out({cmp_4_add_3_30_out[0], cmp_4_add_3_30_out_2}));
  cmp_4_add_3 cmp_4_add_3_31 (
    .in({cmp_4_add_3_30_out_2, adder_1_out_11[0]}), .out({cmp_4_add_3_31_out[0], cmp_4_add_3_31_out_2}));
  cmp_4_add_3 cmp_4_add_3_32 (.in({cmp_4_add_3_28_out_2, cmp_4_add_3_27_out[0]}), .out(cmp_4_add_3_32_out));
  cmp_4_add_3 cmp_4_add_3_33 (
    .in({cmp_4_add_3_27_out_2, cmp_4_add_3_31_out[0]}), .out({cmp_4_add_3_33_out[0], cmp_4_add_3_33_out_2}));
  Hex_Digit_Display hex_digit_display_3 (.value({cmp_4_add_3_32_out[2:0], cmp_4_add_3_33_out[0]}));  // open: dp
  cmp_4_add_3 cmp_4_add_3_34 (
    .in({cmp_4_add_3_31_out_2, adder_1_out_12[0]}), .out({cmp_4_add_3_34_out[0], cmp_4_add_3_34_out_2}));
  Hex_Digit_Display hex_digit_display_4 (.value({cmp_4_add_3_33_out_2, cmp_4_add_3_34_out[0]}));  // open: dp
  Hex_Digit_Display hex_digit_display_5 (.value({cmp_4_add_3_34_out_2, adder_1_out_13[0]}));  // open: dp
endmodule

module cmp_4_add_3 (
  input  [3:0] in,
  output [3:0] out
);

  wire comparator_1_gt;
  wire [3:0] adder_1_out;

  Comparator #(.width(4), .mode("unsigned")) comparator_1 (.a(in), .b(4'b0100), .gt(comparator_1_gt));  // open: eq, lt
  Adder #(.width(4)) adder_1 (.a(in), .b(4'b0011), .out(adder_1_out));  // open: cin, cout
  Multiplexer #(.width(4)) multiplexer_1 (.in0(in), .in1(adder_1_out), .out(out), .sel(comparator_1_gt));  // open: en
endmodule
